# Fritzing sketch wiring (saved by Fritzing 0.9.2b)
breadboards: 1

parts:
  RE1 = Rotary Encoder [package=THT]
  RE2 = Rotary Encoder [package=THT]
  S1 = Pushbutton [package=THT]
  Bauteil1 = Arduino Uno (Rev3)
  LED_table = ws2812b [package="smd 2812b"]

nets:
  GND: RE1.EncoderPinA, RE2.EncoderPinA, S1.leg1, Bauteil1.GND, LED_table.VSS
  N1: RE1.EncoderPinC, Bauteil1.A0
  5V: RE1.EncoderPinB, RE2.EncoderPinB, Bauteil1.5V, LED_table.VDD
  N2: RE2.EncoderPinC, Bauteil1.A1
  N3: S1.leg0, Bauteil1.D5_PWM
  N4: Bauteil1.D6_PWM, LED_table.DIN
